// Logisim project micro.circ as structural Verilog: 1 circuit, main circuit EV20_Superescalar
module EV20_Superescalar (
  input  in_1
);

  wire ALU_is_done, ALU_is_free, ALU_Pipeline_p17, ALUALULAU_cyout, and_1_out, and_2_out, and_3_out,
       and_4_out, bloque1_bsr_1_preload, bloque1_jmp_1_preload, CLK, CLK2, CLK3, CLK4, CYin, HOLD,
       instruction2register_1_p2, instruction2register_1_p3, instruction2register_1_p4,
       instruction2register_1_p5, LatchMemEnable, LoadStore_p17, MEM_is_done, mem_is_free, nor_1_out,
       not_1_out, not_2_out, not_3_out, not_4_out, or_1_out, or_2_out, or_3_out, or_4_out,
       pipeline_register_2_p7, pipeline_register_viewer_1_a_is_enabled,
       pipeline_register_viewer_1_b_is_enabled, pipeline_register_viewer_1_c_is_enabled,
       pipeline_register_viewer_2_a_is_enabled, pipeline_register_viewer_2_b_is_enabled,
       pipeline_register_viewer_2_c_is_enabled, pipeline_register_viewer_3_a_is_enabled,
       pipeline_register_viewer_3_b_is_enabled, pipeline_register_viewer_3_c_is_enabled,
       pipeline_register_viewer_4_a_is_enabled, pipeline_register_viewer_4_b_is_enabled,
       pipeline_register_viewer_4_c_is_enabled, register_1_q, register_2_q,
       register_bank_viewer_1_a_is_enabled, register_bank_viewer_1_b_is_enabled,
       register_bank_viewer_1_c_is_enabled, uc1_1_p5, uc1_1_p6, UC1_HOLD, undriven, undriven_2, undriven_3,
       undriven_5;
  wire [1:0] ALU_Pipeline_p13, MREtapa2Pipeline, MRMW, pipeline_register_1_p13, pipeline_register_1_p15,
       undriven_4;
  wire [2:0] ProgramCounterReg_pc_2;
  wire [3:0] ALU_Pipeline_p12, output_ports_viewer_1_hex_disp_0_0, output_ports_viewer_1_hex_disp_0_1,
       output_ports_viewer_1_hex_disp_0_2, output_ports_viewer_1_hex_disp_0_3,
       output_ports_viewer_1_hex_disp_1_0, output_ports_viewer_1_hex_disp_1_1,
       output_ports_viewer_1_hex_disp_1_2, output_ports_viewer_1_hex_disp_1_3, pipeline_register_1_p12,
       pipeline_register_viewer_1_a_lsn, pipeline_register_viewer_1_a_msn, pipeline_register_viewer_1_b0,
       pipeline_register_viewer_1_b1, pipeline_register_viewer_1_b2, pipeline_register_viewer_1_b3,
       pipeline_register_viewer_1_b4, pipeline_register_viewer_1_b5, pipeline_register_viewer_1_b6,
       pipeline_register_viewer_1_b7, pipeline_register_viewer_1_b8, pipeline_register_viewer_1_b9,
       pipeline_register_viewer_1_b10, pipeline_register_viewer_1_b11, pipeline_register_viewer_1_b12,
       pipeline_register_viewer_1_b13, pipeline_register_viewer_1_b14, pipeline_register_viewer_1_b15,
       pipeline_register_viewer_1_b16, pipeline_register_viewer_1_b_lsn, pipeline_register_viewer_1_b_msn,
       pipeline_register_viewer_1_c_lsn, pipeline_register_viewer_1_c_msn, pipeline_register_viewer_2_a_lsn,
       pipeline_register_viewer_2_a_msn, pipeline_register_viewer_2_b0, pipeline_register_viewer_2_b1,
       pipeline_register_viewer_2_b2, pipeline_register_viewer_2_b3, pipeline_register_viewer_2_b4,
       pipeline_register_viewer_2_b5, pipeline_register_viewer_2_b6, pipeline_register_viewer_2_b7,
       pipeline_register_viewer_2_b8, pipeline_register_viewer_2_b9, pipeline_register_viewer_2_b10,
       pipeline_register_viewer_2_b11, pipeline_register_viewer_2_b12, pipeline_register_viewer_2_b13,
       pipeline_register_viewer_2_b14, pipeline_register_viewer_2_b15, pipeline_register_viewer_2_b16,
       pipeline_register_viewer_2_b_lsn, pipeline_register_viewer_2_b_msn, pipeline_register_viewer_2_c_lsn,
       pipeline_register_viewer_2_c_msn, pipeline_register_viewer_3_a_lsn, pipeline_register_viewer_3_a_msn,
       pipeline_register_viewer_3_b0, pipeline_register_viewer_3_b1, pipeline_register_viewer_3_b2,
       pipeline_register_viewer_3_b3, pipeline_register_viewer_3_b4, pipeline_register_viewer_3_b5,
       pipeline_register_viewer_3_b6, pipeline_register_viewer_3_b7, pipeline_register_viewer_3_b8,
       pipeline_register_viewer_3_b9, pipeline_register_viewer_3_b10, pipeline_register_viewer_3_b11,
       pipeline_register_viewer_3_b12, pipeline_register_viewer_3_b13, pipeline_register_viewer_3_b14,
       pipeline_register_viewer_3_b15, pipeline_register_viewer_3_b16, pipeline_register_viewer_3_b_lsn,
       pipeline_register_viewer_3_b_msn, pipeline_register_viewer_3_c_lsn, pipeline_register_viewer_3_c_msn,
       pipeline_register_viewer_4_a_lsn, pipeline_register_viewer_4_a_msn, pipeline_register_viewer_4_b0,
       pipeline_register_viewer_4_b1, pipeline_register_viewer_4_b2, pipeline_register_viewer_4_b3,
       pipeline_register_viewer_4_b4, pipeline_register_viewer_4_b5, pipeline_register_viewer_4_b6,
       pipeline_register_viewer_4_b7, pipeline_register_viewer_4_b8, pipeline_register_viewer_4_b9,
       pipeline_register_viewer_4_b10, pipeline_register_viewer_4_b11, pipeline_register_viewer_4_b12,
       pipeline_register_viewer_4_b13, pipeline_register_viewer_4_b14, pipeline_register_viewer_4_b15,
       pipeline_register_viewer_4_b16, pipeline_register_viewer_4_b_lsn, pipeline_register_viewer_4_b_msn,
       pipeline_register_viewer_4_c_lsn, pipeline_register_viewer_4_c_msn,
       register_bank_viewer_1_a_address_n0, register_bank_viewer_1_a_address_n1,
       register_bank_viewer_1_a_address_n2, register_bank_viewer_1_a_address_n3,
       register_bank_viewer_1_a_data_lsn, register_bank_viewer_1_a_data_msn,
       register_bank_viewer_1_b_address_n0, register_bank_viewer_1_b_address_n1,
       register_bank_viewer_1_b_address_n2, register_bank_viewer_1_b_address_n3,
       register_bank_viewer_1_b_data_lsn, register_bank_viewer_1_b_data_msn,
       register_bank_viewer_1_c_address_n0, register_bank_viewer_1_c_address_n1,
       register_bank_viewer_1_c_address_n2, register_bank_viewer_1_c_address_n3,
       register_bank_viewer_1_c_data_lsn, register_bank_viewer_1_c_data_msn;
  wire [5:0] A_Etapa1, ALU_Pipeline_p16, ALU_Pipeline_p18, ALU_Pipeline_p19, B_Etapa1, C_Etapa1, C_Etapa2Alu,
       C_Etapa2Mem, C_Etapa3, judge_1_a_bus, judge_1_b_bus, judge_1_c_bus, LoadStore_p18, LoadStore_p19,
       pipeline_register_1_p16, pipeline_register_2_p16, pipeline_register_2_p17;
  wire [7:0] clk_edge_viewer_1_out_2, clk_edge_viewer_1_out_3, clk_edge_viewer_1_out_4,
       clk_edge_viewer_1_out_5, clk_edge_viewer_1_out_6, clk_edge_viewer_1_out_7, clk_edge_viewer_1_out_8,
       clk_edge_viewer_1_out_9, ProgramCounterReg_pc, uc2_viewer_1_out_2, uc2_viewer_1_out_3,
       uc2_viewer_1_out_4, uc2_viewer_1_out_5, uc2_viewer_1_out_6, uc2_viewer_1_out_7, uc2_viewer_1_out_8,
       uc2_viewer_1_out_9, uc2_viewer_2_out_2, uc2_viewer_2_out_3, uc2_viewer_2_out_4, uc2_viewer_2_out_5,
       uc2_viewer_2_out_6, uc2_viewer_2_out_7, uc2_viewer_2_out_8, uc2_viewer_2_out_9;
  wire [8:8] ALU_Pipeline_p14, pipeline_register_1_p14;
  wire [9:0] pipeline_register_1_p17, register_3_q;
  wire [10:0] bloque1_bsr_1_next_address;
  wire [14:0] judge_1_reg_out, LoadStore_p16, MicroInstructionROM_microinstruction, pipeline_register_2_p15;
  wire [15:0] ALU_RESULT, ALUALULAU_z, BusA_ALU_q, BusA_LS_q, BusB_ALU_q, Constant_K_q, data_1_datamemout,
       dipswitch_1_sw16, dipswitch_2_sw16, instruction2register_1_p6, multiplexer_1_out, reg_C_write,
       register_6_q, register_bank_1_register_out_a_data, register_bank_1_register_out_b_data, undriven_6,
       undriven_7;
  wire [23:0] BBUS, ProgramMemory_data;
  wire [31:0] output_ports_viewer_1_mat_0_col_0, output_ports_viewer_1_mat_0_col_0_2,
       output_ports_viewer_1_mat_0_col_0_3, output_ports_viewer_1_mat_0_col_0_4,
       output_ports_viewer_1_mat_0_col_0_5, output_ports_viewer_1_mat_0_col_0_6,
       output_ports_viewer_1_mat_0_col_0_7, output_ports_viewer_1_mat_0_col_0_8,
       output_ports_viewer_1_mat_0_col_1, output_ports_viewer_1_mat_0_col_1_2,
       output_ports_viewer_1_mat_0_col_1_3, output_ports_viewer_1_mat_0_col_1_4,
       output_ports_viewer_1_mat_0_col_1_5, output_ports_viewer_1_mat_0_col_1_6,
       output_ports_viewer_1_mat_0_col_1_7, output_ports_viewer_1_mat_0_col_1_8,
       output_ports_viewer_1_mat_0_col_2, output_ports_viewer_1_mat_0_col_2_2,
       output_ports_viewer_1_mat_0_col_2_3, output_ports_viewer_1_mat_0_col_2_4,
       output_ports_viewer_1_mat_0_col_2_5, output_ports_viewer_1_mat_0_col_2_6,
       output_ports_viewer_1_mat_0_col_2_7, output_ports_viewer_1_mat_0_col_2_8,
       output_ports_viewer_1_mat_0_col_3, output_ports_viewer_1_mat_0_col_3_2,
       output_ports_viewer_1_mat_0_col_3_3, output_ports_viewer_1_mat_0_col_3_4,
       output_ports_viewer_1_mat_0_col_3_5, output_ports_viewer_1_mat_0_col_3_6,
       output_ports_viewer_1_mat_0_col_3_7, output_ports_viewer_1_mat_0_col_3_8,
       output_ports_viewer_1_mat_1_col_0, output_ports_viewer_1_mat_1_col_0_2,
       output_ports_viewer_1_mat_1_col_0_3, output_ports_viewer_1_mat_1_col_0_4,
       output_ports_viewer_1_mat_1_col_0_5, output_ports_viewer_1_mat_1_col_0_6,
       output_ports_viewer_1_mat_1_col_0_7, output_ports_viewer_1_mat_1_col_0_8,
       output_ports_viewer_1_mat_1_col_1, output_ports_viewer_1_mat_1_col_1_2,
       output_ports_viewer_1_mat_1_col_1_3, output_ports_viewer_1_mat_1_col_1_4,
       output_ports_viewer_1_mat_1_col_1_5, output_ports_viewer_1_mat_1_col_1_6,
       output_ports_viewer_1_mat_1_col_1_7, output_ports_viewer_1_mat_1_col_1_8,
       output_ports_viewer_1_mat_1_col_2, output_ports_viewer_1_mat_1_col_2_2,
       output_ports_viewer_1_mat_1_col_2_3, output_ports_viewer_1_mat_1_col_2_4,
       output_ports_viewer_1_mat_1_col_2_5, output_ports_viewer_1_mat_1_col_2_6,
       output_ports_viewer_1_mat_1_col_2_7, output_ports_viewer_1_mat_1_col_2_8,
       output_ports_viewer_1_mat_1_col_3, output_ports_viewer_1_mat_1_col_3_2,
       output_ports_viewer_1_mat_1_col_3_3, output_ports_viewer_1_mat_1_col_3_4,
       output_ports_viewer_1_mat_1_col_3_5, output_ports_viewer_1_mat_1_col_3_6,
       output_ports_viewer_1_mat_1_col_3_7, output_ports_viewer_1_mat_1_col_3_8;

  Hex_Digit_Display hex_digit_display_1 (.value({1'b0, ProgramCounterReg_pc_2}));  // open: dp
  // Probe on {ProgramCounterReg_pc_2, ProgramCounterReg_pc}
  ROM #(.addrWidth(11), .dataWidth(24)) ProgramMemory (
    .addr({ProgramCounterReg_pc_2, ProgramCounterReg_pc}), .data(ProgramMemory_data));
  Clock sysclk ();  // open: out
  Hex_Digit_Display hex_digit_display_2 (.value(ProgramCounterReg_pc[3:0]));  // open: dp
  Hex_Digit_Display hex_digit_display_3 (.value(ProgramCounterReg_pc[7:4]));  // open: dp
  Bloque1_bsr bloque1_bsr_1 (
    .opcode(BBUS[23:16]), .displacement(BBUS[15:5]), .Preload(bloque1_bsr_1_preload),
    .next_address(bloque1_bsr_1_next_address), .PC({ProgramCounterReg_pc_2, ProgramCounterReg_pc}), .CLK(CLK));
  // Probe on HOLD
  // Probe on UC1_HOLD
  // Probe on CLK
  // Probe on undriven
  // Probe on undriven_2
  // Probe on undriven_3
  // Probe on undriven_4[1]
  // Probe on undriven_4[0]
  // Probe on undriven_5
  ClockGenerator clocks (.Auto(1'b1), .ManualCLK(in_1), .CLK(CLK), .CLK2(CLK2), .CLK3(CLK3), .CLK4(CLK4));
  // Probe on ProgramMemory_data
  Bloque1_jmp bloque1_jmp_1 (
    .Preload(bloque1_jmp_1_preload), .register_to_test(register_bank_1_register_out_a_data), .CY(CYin),
    .opcode(BBUS[23:16]), .nxt_address(BBUS[15:5]), .next_address(bloque1_bsr_1_next_address));
  or or_1 (or_1_out, HOLD, UC1_HOLD);
  // Probe on bloque1_bsr_1_next_address
  or or_2 (or_2_out, bloque1_jmp_1_preload, bloque1_bsr_1_preload);
  Register #(.width(24)) InstructionRegister (.D(ProgramMemory_data), .clk(CLK), .Q(BBUS));  // open: en, clr
  PCreg ProgramCounterReg (
    .PC({ProgramCounterReg_pc_2, ProgramCounterReg_pc}), .HOLD(or_1_out), .Preload(or_2_out), .CLK1(CLK),
    .displacement_or_address(bloque1_bsr_1_next_address));
  // Probe on BBUS
  Hex_Digit_Display hex_digit_display_4 (.value(register_bank_viewer_1_c_data_msn));  // open: dp
  Hex_Digit_Display hex_digit_display_5 (.value(register_bank_viewer_1_c_data_lsn));  // open: dp
  DipSwitch #(.number(16)) dipswitch_1 (
    .sw1(dipswitch_1_sw16[15]), .sw2(dipswitch_1_sw16[14]), .sw3(dipswitch_1_sw16[13]),
    .sw4(dipswitch_1_sw16[12]), .sw5(dipswitch_1_sw16[11]), .sw6(dipswitch_1_sw16[10]),
    .sw7(dipswitch_1_sw16[9]), .sw8(dipswitch_1_sw16[8]), .sw9(dipswitch_1_sw16[7]),
    .sw10(dipswitch_1_sw16[6]), .sw11(dipswitch_1_sw16[5]), .sw12(dipswitch_1_sw16[4]),
    .sw13(dipswitch_1_sw16[3]), .sw14(dipswitch_1_sw16[2]), .sw15(dipswitch_1_sw16[1]),
    .sw16(dipswitch_1_sw16[0]));
  or or_3 (or_3_out, HOLD, UC1_HOLD);
  LED led_1 (.in(register_bank_viewer_1_c_is_enabled));
  Hex_Digit_Display hex_digit_display_6 (.value(register_bank_viewer_1_c_address_n3));  // open: dp
  Hex_Digit_Display hex_digit_display_7 (.value(register_bank_viewer_1_c_address_n2));  // open: dp
  DotMatrix #(.matrixcols(32), .matrixrows(32)) dotmatrix_1 (
    .col0(output_ports_viewer_1_mat_0_col_3_2), .col1(output_ports_viewer_1_mat_0_col_3_4),
    .col2(output_ports_viewer_1_mat_0_col_3_6), .col3(output_ports_viewer_1_mat_0_col_3_8),
    .col4(output_ports_viewer_1_mat_0_col_3), .col5(output_ports_viewer_1_mat_0_col_3_3),
    .col6(output_ports_viewer_1_mat_0_col_3_5), .col7(output_ports_viewer_1_mat_0_col_3_7),
    .col8(output_ports_viewer_1_mat_0_col_2), .col9(output_ports_viewer_1_mat_0_col_2_3),
    .col10(output_ports_viewer_1_mat_0_col_2_5), .col11(output_ports_viewer_1_mat_0_col_2_7),
    .col12(output_ports_viewer_1_mat_0_col_2_2), .col13(output_ports_viewer_1_mat_0_col_2_4),
    .col14(output_ports_viewer_1_mat_0_col_2_6), .col15(output_ports_viewer_1_mat_0_col_2_8),
    .col16(output_ports_viewer_1_mat_0_col_1), .col17(output_ports_viewer_1_mat_0_col_1_3),
    .col18(output_ports_viewer_1_mat_0_col_1_5), .col19(output_ports_viewer_1_mat_0_col_1_7),
    .col20(output_ports_viewer_1_mat_0_col_1_2), .col21(output_ports_viewer_1_mat_0_col_1_4),
    .col22(output_ports_viewer_1_mat_0_col_1_6), .col23(output_ports_viewer_1_mat_0_col_1_8),
    .col24(output_ports_viewer_1_mat_0_col_0_2), .col25(output_ports_viewer_1_mat_0_col_0_4),
    .col26(output_ports_viewer_1_mat_0_col_0_6), .col27(output_ports_viewer_1_mat_0_col_0_8),
    .col28(output_ports_viewer_1_mat_0_col_0), .col29(output_ports_viewer_1_mat_0_col_0_3),
    .col30(output_ports_viewer_1_mat_0_col_0_5), .col31(output_ports_viewer_1_mat_0_col_0_7));
  clk_edge_viewer clk_edge_viewer_1 (
    .out_7(clk_edge_viewer_1_out_7), .out_4(clk_edge_viewer_1_out_4), .out_5(clk_edge_viewer_1_out_5),
    .out_2(clk_edge_viewer_1_out_2), .out_3(clk_edge_viewer_1_out_3), .out_8(clk_edge_viewer_1_out_8),
    .in_1(CLK2), .out_9(clk_edge_viewer_1_out_9), .out_6(clk_edge_viewer_1_out_6));
  UC2_viewer uc2_viewer_1 (
    .out_7(uc2_viewer_1_out_7), .out_5(uc2_viewer_1_out_5), .out_3(uc2_viewer_1_out_3), .hold(UC1_HOLD),
    .out_6(uc2_viewer_1_out_6), .out_9(uc2_viewer_1_out_9), .out_8(uc2_viewer_1_out_8),
    .out_2(uc2_viewer_1_out_2), .out_4(uc2_viewer_1_out_4));
  DotMatrix #(.matrixcols(8), .matrixrows(8)) dotmatrix_2 (
    .col0(uc2_viewer_1_out_2), .col1(uc2_viewer_1_out_3), .col2(uc2_viewer_1_out_4),
    .col3(uc2_viewer_1_out_5), .col4(uc2_viewer_1_out_6), .col5(uc2_viewer_1_out_7),
    .col6(uc2_viewer_1_out_8), .col7(uc2_viewer_1_out_9));
  Hex_Digit_Display hex_digit_display_8 (.value(register_bank_viewer_1_c_address_n1));  // open: dp
  Hex_Digit_Display hex_digit_display_9 (.value(register_bank_viewer_1_c_address_n0));  // open: dp
  DipSwitch #(.number(16)) dipswitch_2 (
    .sw1(dipswitch_2_sw16[15]), .sw2(dipswitch_2_sw16[14]), .sw3(dipswitch_2_sw16[13]),
    .sw4(dipswitch_2_sw16[12]), .sw5(dipswitch_2_sw16[11]), .sw6(dipswitch_2_sw16[10]),
    .sw7(dipswitch_2_sw16[9]), .sw8(dipswitch_2_sw16[8]), .sw9(dipswitch_2_sw16[7]),
    .sw10(dipswitch_2_sw16[6]), .sw11(dipswitch_2_sw16[5]), .sw12(dipswitch_2_sw16[4]),
    .sw13(dipswitch_2_sw16[3]), .sw14(dipswitch_2_sw16[2]), .sw15(dipswitch_2_sw16[1]),
    .sw16(dipswitch_2_sw16[0]));
  DotMatrix #(.matrixcols(8), .matrixrows(8)) dotmatrix_3 (
    .col0(clk_edge_viewer_1_out_2), .col1(clk_edge_viewer_1_out_3), .col2(clk_edge_viewer_1_out_4),
    .col3(clk_edge_viewer_1_out_5), .col4(clk_edge_viewer_1_out_6), .col5(clk_edge_viewer_1_out_7),
    .col6(clk_edge_viewer_1_out_8), .col7(clk_edge_viewer_1_out_9));
  Hex_Digit_Display hex_digit_display_10 (.value(register_bank_viewer_1_a_data_msn));  // open: dp
  Hex_Digit_Display hex_digit_display_11 (.value(output_ports_viewer_1_hex_disp_0_3));  // open: dp
  output_ports_viewer output_ports_viewer_1 (
    .PO0(undriven_7), .MAT_1_COL_3(output_ports_viewer_1_mat_1_col_3),
    .hex_disp_0_2(output_ports_viewer_1_hex_disp_0_2), .hex_disp_1_2(output_ports_viewer_1_hex_disp_1_2),
    .MAT_0_COL_3(output_ports_viewer_1_mat_0_col_3), .MAT_0_COL_0_5(output_ports_viewer_1_mat_0_col_0_5),
    .MAT_0_COL_3_7(output_ports_viewer_1_mat_0_col_3_7), .MAT_0_COL_1_7(output_ports_viewer_1_mat_0_col_1_7),
    .MAT_0_COL_2_5(output_ports_viewer_1_mat_0_col_2_5), .MAT_0_COL_1(output_ports_viewer_1_mat_0_col_1),
    .MAT_0_COL_1_3(output_ports_viewer_1_mat_0_col_1_3), .MAT_0_COL_2_3(output_ports_viewer_1_mat_0_col_2_3),
    .MAT_0_COL_0(output_ports_viewer_1_mat_0_col_0), .MAT_0_COL_3_5(output_ports_viewer_1_mat_0_col_3_5),
    .MAT_0_COL_0_7(output_ports_viewer_1_mat_0_col_0_7), .hex_disp_0_0(output_ports_viewer_1_hex_disp_0_0),
    .hex_disp_1_1(output_ports_viewer_1_hex_disp_1_1), .hex_disp_0_3(output_ports_viewer_1_hex_disp_0_3),
    .MAT_1_COL_3_3(output_ports_viewer_1_mat_1_col_3_3), .MAT_1_COL_3_7(output_ports_viewer_1_mat_1_col_3_7),
    .MAT_1_COL_3_5(output_ports_viewer_1_mat_1_col_3_5), .PO1(undriven_6),
    .hex_disp_1_0(output_ports_viewer_1_hex_disp_1_0), .hex_disp_0_1(output_ports_viewer_1_hex_disp_0_1),
    .hex_disp_1_3(output_ports_viewer_1_hex_disp_1_3), .MAT_0_COL_3_3(output_ports_viewer_1_mat_0_col_3_3),
    .MAT_0_COL_0_3(output_ports_viewer_1_mat_0_col_0_3), .MAT_0_COL_2(output_ports_viewer_1_mat_0_col_2),
    .MAT_0_COL_1_5(output_ports_viewer_1_mat_0_col_1_5), .MAT_0_COL_2_7(output_ports_viewer_1_mat_0_col_2_7),
    .MAT_1_COL_2(output_ports_viewer_1_mat_1_col_2), .MAT_1_COL_2_3(output_ports_viewer_1_mat_1_col_2_3),
    .MAT_1_COL_2_5(output_ports_viewer_1_mat_1_col_2_5), .MAT_1_COL_2_7(output_ports_viewer_1_mat_1_col_2_7),
    .MAT_1_COL_1(output_ports_viewer_1_mat_1_col_1), .MAT_1_COL_1_3(output_ports_viewer_1_mat_1_col_1_3),
    .MAT_1_COL_1_5(output_ports_viewer_1_mat_1_col_1_5), .MAT_1_COL_1_7(output_ports_viewer_1_mat_1_col_1_7),
    .MAT_1_COL_0(output_ports_viewer_1_mat_1_col_0), .MAT_1_COL_0_3(output_ports_viewer_1_mat_1_col_0_3),
    .MAT_1_COL_0_5(output_ports_viewer_1_mat_1_col_0_5), .MAT_1_COL_0_7(output_ports_viewer_1_mat_1_col_0_7),
    .MAT_0_COL_3_2(output_ports_viewer_1_mat_0_col_3_2), .MAT_0_COL_3_4(output_ports_viewer_1_mat_0_col_3_4),
    .MAT_0_COL_3_6(output_ports_viewer_1_mat_0_col_3_6), .MAT_0_COL_3_8(output_ports_viewer_1_mat_0_col_3_8),
    .MAT_0_COL_2_2(output_ports_viewer_1_mat_0_col_2_2), .MAT_0_COL_2_4(output_ports_viewer_1_mat_0_col_2_4),
    .MAT_0_COL_2_6(output_ports_viewer_1_mat_0_col_2_6), .MAT_0_COL_2_8(output_ports_viewer_1_mat_0_col_2_8),
    .MAT_0_COL_1_2(output_ports_viewer_1_mat_0_col_1_2), .MAT_0_COL_1_4(output_ports_viewer_1_mat_0_col_1_4),
    .MAT_0_COL_1_6(output_ports_viewer_1_mat_0_col_1_6), .MAT_0_COL_1_8(output_ports_viewer_1_mat_0_col_1_8),
    .MAT_0_COL_0_2(output_ports_viewer_1_mat_0_col_0_2), .MAT_0_COL_0_4(output_ports_viewer_1_mat_0_col_0_4),
    .MAT_0_COL_0_6(output_ports_viewer_1_mat_0_col_0_6), .MAT_0_COL_0_8(output_ports_viewer_1_mat_0_col_0_8),
    .MAT_1_COL_3_2(output_ports_viewer_1_mat_1_col_3_2), .MAT_1_COL_3_4(output_ports_viewer_1_mat_1_col_3_4),
    .MAT_1_COL_3_6(output_ports_viewer_1_mat_1_col_3_6), .MAT_1_COL_3_8(output_ports_viewer_1_mat_1_col_3_8),
    .MAT_1_COL_2_2(output_ports_viewer_1_mat_1_col_2_2), .MAT_1_COL_2_4(output_ports_viewer_1_mat_1_col_2_4),
    .MAT_1_COL_2_6(output_ports_viewer_1_mat_1_col_2_6), .MAT_1_COL_2_8(output_ports_viewer_1_mat_1_col_2_8),
    .MAT_1_COL_1_2(output_ports_viewer_1_mat_1_col_1_2), .MAT_1_COL_1_4(output_ports_viewer_1_mat_1_col_1_4),
    .MAT_1_COL_1_6(output_ports_viewer_1_mat_1_col_1_6), .MAT_1_COL_1_8(output_ports_viewer_1_mat_1_col_1_8),
    .MAT_1_COL_0_2(output_ports_viewer_1_mat_1_col_0_2), .MAT_1_COL_0_4(output_ports_viewer_1_mat_1_col_0_4),
    .MAT_1_COL_0_6(output_ports_viewer_1_mat_1_col_0_6), .MAT_1_COL_0_8(output_ports_viewer_1_mat_1_col_0_8));
  // instruction2register instruction2register_1: pin names not known; wires that end beside it: BBUS, instruction2register_1_p2, instruction2register_1_p3, instruction2register_1_p4, instruction2register_1_p5, instruction2register_1_p6
  Hex_Digit_Display hex_digit_display_12 (.value(register_bank_viewer_1_a_data_lsn));  // open: dp
  Hex_Digit_Display hex_digit_display_13 (.value(register_bank_viewer_1_a_address_n3));  // open: dp
  Hex_Digit_Display hex_digit_display_14 (.value(output_ports_viewer_1_hex_disp_0_2));  // open: dp
  Hex_Digit_Display hex_digit_display_15 (.value(output_ports_viewer_1_hex_disp_0_1));  // open: dp
  Micro_Instruction_ROM MicroInstructionROM (
    .Instruction(BBUS), .MicroInstruction(MicroInstructionROM_microinstruction));
  LED led_2 (.in(register_bank_viewer_1_a_is_enabled));
  register_bank_viewer register_bank_viewer_1 (
    .A_is_enabled(register_bank_viewer_1_a_is_enabled), .C_address_N2(register_bank_viewer_1_c_address_n2),
    .B_data_out(B_Etapa1), .B_data_LSN(register_bank_viewer_1_b_data_lsn),
    .A_address(register_bank_1_register_out_a_data), .A_address_N2(register_bank_viewer_1_a_address_n2),
    .C_address_N0(register_bank_viewer_1_c_address_n0), .C_is_enabled(register_bank_viewer_1_c_is_enabled),
    .B_address(register_bank_1_register_out_b_data), .C_address_N3(register_bank_viewer_1_c_address_n3),
    .B_is_enabled(register_bank_viewer_1_b_is_enabled), .C_address_N1(register_bank_viewer_1_c_address_n1),
    .B_address_N2(register_bank_viewer_1_b_address_n2), .A_address_N0(register_bank_viewer_1_a_address_n0),
    .C_data_out(C_Etapa3), .A_address_N1(register_bank_viewer_1_a_address_n1), .C_address(reg_C_write),
    .B_address_N0(register_bank_viewer_1_b_address_n0), .A_data_out(A_Etapa1),
    .C_data_MSN(register_bank_viewer_1_c_data_msn), .B_address_N3(register_bank_viewer_1_b_address_n3),
    .B_address_N1(register_bank_viewer_1_b_address_n1), .C_data_LSN(register_bank_viewer_1_c_data_lsn),
    .A_address_N3(register_bank_viewer_1_a_address_n3), .A_data_LSN(register_bank_viewer_1_a_data_lsn),
    .A_data_MSN(register_bank_viewer_1_a_data_msn), .B_data_MSN(register_bank_viewer_1_b_data_msn));
  Hex_Digit_Display hex_digit_display_16 (.value(register_bank_viewer_1_a_address_n1));  // open: dp
  Hex_Digit_Display hex_digit_display_17 (.value(register_bank_viewer_1_a_address_n2));  // open: dp
  DotMatrix #(.matrixcols(32), .matrixrows(32)) dotmatrix_4 (
    .col0(output_ports_viewer_1_mat_1_col_3), .col1(output_ports_viewer_1_mat_1_col_3_3),
    .col2(output_ports_viewer_1_mat_1_col_3_5), .col3(output_ports_viewer_1_mat_1_col_3_7),
    .col4(output_ports_viewer_1_mat_1_col_3_2), .col5(output_ports_viewer_1_mat_1_col_3_4),
    .col6(output_ports_viewer_1_mat_1_col_3_6), .col7(output_ports_viewer_1_mat_1_col_3_8),
    .col8(output_ports_viewer_1_mat_1_col_2), .col9(output_ports_viewer_1_mat_1_col_2_3),
    .col10(output_ports_viewer_1_mat_1_col_2_5), .col11(output_ports_viewer_1_mat_1_col_2_7),
    .col12(output_ports_viewer_1_mat_1_col_2_2), .col13(output_ports_viewer_1_mat_1_col_2_4),
    .col14(output_ports_viewer_1_mat_1_col_2_6), .col15(output_ports_viewer_1_mat_1_col_2_8),
    .col16(output_ports_viewer_1_mat_1_col_1), .col17(output_ports_viewer_1_mat_1_col_1_3),
    .col18(output_ports_viewer_1_mat_1_col_1_5), .col19(output_ports_viewer_1_mat_1_col_1_7),
    .col20(output_ports_viewer_1_mat_1_col_1_2), .col21(output_ports_viewer_1_mat_1_col_1_4),
    .col22(output_ports_viewer_1_mat_1_col_1_6), .col23(output_ports_viewer_1_mat_1_col_1_8),
    .col24(output_ports_viewer_1_mat_1_col_0), .col25(output_ports_viewer_1_mat_1_col_0_3),
    .col26(output_ports_viewer_1_mat_1_col_0_5), .col27(output_ports_viewer_1_mat_1_col_0_7),
    .col28(output_ports_viewer_1_mat_1_col_0_2), .col29(output_ports_viewer_1_mat_1_col_0_4),
    .col30(output_ports_viewer_1_mat_1_col_0_6), .col31(output_ports_viewer_1_mat_1_col_0_8));
  Hex_Digit_Display hex_digit_display_18 (.value(output_ports_viewer_1_hex_disp_0_0));  // open: dp
  DotMatrix #(.matrixcols(17), .matrixrows(4)) dotmatrix_5 (
    .col0(pipeline_register_viewer_1_b16), .col1(pipeline_register_viewer_1_b15),
    .col2(pipeline_register_viewer_1_b14), .col3(pipeline_register_viewer_1_b13),
    .col4(pipeline_register_viewer_1_b12), .col5(pipeline_register_viewer_1_b11),
    .col6(pipeline_register_viewer_1_b10), .col7(pipeline_register_viewer_1_b9),
    .col8(pipeline_register_viewer_1_b8), .col9(pipeline_register_viewer_1_b7),
    .col10(pipeline_register_viewer_1_b6), .col11(pipeline_register_viewer_1_b5),
    .col12(pipeline_register_viewer_1_b4), .col13(pipeline_register_viewer_1_b3),
    .col14(pipeline_register_viewer_1_b2), .col15(pipeline_register_viewer_1_b1),
    .col16(pipeline_register_viewer_1_b0));
  pipeline_register_viewer pipeline_register_viewer_1 (
    .b7(pipeline_register_viewer_1_b7), .b12(pipeline_register_viewer_1_b12),
    .A_is_enabled(pipeline_register_viewer_1_a_is_enabled), .A_LSN(pipeline_register_viewer_1_a_lsn),
    .b16(pipeline_register_viewer_1_b16), .b11(pipeline_register_viewer_1_b11),
    .b2(pipeline_register_viewer_1_b2), .b3(pipeline_register_viewer_1_b3),
    .b8(pipeline_register_viewer_1_b8), .C_in(C_Etapa1), .B_MSN(pipeline_register_viewer_1_b_msn),
    .microinstruction({pipeline_register_1_p12, pipeline_register_1_p13, pipeline_register_1_p14[8], pipeline_register_1_p15, pipeline_register_1_p16}),
    .b15(pipeline_register_viewer_1_b15), .b14(pipeline_register_viewer_1_b14),
    .b1(pipeline_register_viewer_1_b1), .b4(pipeline_register_viewer_1_b4),
    .b13(pipeline_register_viewer_1_b13), .B_in(B_Etapa1),
    .B_is_enabled(pipeline_register_viewer_1_b_is_enabled), .A_in(A_Etapa1),
    .b10(pipeline_register_viewer_1_b10), .b5(pipeline_register_viewer_1_b5),
    .b0(pipeline_register_viewer_1_b0), .b9(pipeline_register_viewer_1_b9),
    .b6(pipeline_register_viewer_1_b6), .A_MSN(pipeline_register_viewer_1_a_msn),
    .B_LSN(pipeline_register_viewer_1_b_lsn), .C_is_enabled(pipeline_register_viewer_1_c_is_enabled),
    .C_MSN(pipeline_register_viewer_1_c_msn), .C_LSN(pipeline_register_viewer_1_c_lsn));
  // Probe on MicroInstructionROM_microinstruction[14:11]
  // Probe on MicroInstructionROM_microinstruction[10:9]
  // Probe on MicroInstructionROM_microinstruction[8]
  // Probe on MicroInstructionROM_microinstruction[7]
  // Probe on MicroInstructionROM_microinstruction[6]
  // Probe on MicroInstructionROM_microinstruction[5:0]
  Hex_Digit_Display hex_digit_display_19 (.value(register_bank_viewer_1_a_address_n0));  // open: dp
  Hex_Digit_Display hex_digit_display_20 (.value(output_ports_viewer_1_hex_disp_1_3));  // open: dp
  Hex_Digit_Display hex_digit_display_21 (.value(register_bank_viewer_1_b_data_msn));  // open: dp
  Hex_Digit_Display hex_digit_display_22 (.value(output_ports_viewer_1_hex_disp_1_2));  // open: dp
  Hex_Digit_Display hex_digit_display_23 (.value(output_ports_viewer_1_hex_disp_1_1));  // open: dp
  Hex_Digit_Display hex_digit_display_24 (.value(register_bank_viewer_1_b_data_lsn));  // open: dp
  Hex_Digit_Display hex_digit_display_25 (.value(register_bank_viewer_1_b_address_n3));  // open: dp
  Hex_Digit_Display hex_digit_display_26 (.value(output_ports_viewer_1_hex_disp_1_0));  // open: dp
  Hex_Digit_Display hex_digit_display_27 (.value(pipeline_register_viewer_1_c_msn));  // open: dp
  not not_1 (not_1_out, MEM_is_done);
  LED led_3 (.in(register_bank_viewer_1_b_is_enabled));
  Hex_Digit_Display hex_digit_display_28 (.value(register_bank_viewer_1_b_address_n2));  // open: dp
  Hex_Digit_Display hex_digit_display_29 (.value(register_bank_viewer_1_b_address_n1));  // open: dp
  LED led_4 (.in(pipeline_register_viewer_1_c_is_enabled));
  Hex_Digit_Display hex_digit_display_30 (.value(pipeline_register_viewer_1_c_lsn));  // open: dp
  // Probe on pipeline_register_1_p12
  // Pipeline_register pipeline_register_1: pin names not known; wires that end beside it: MicroInstructionROM_microinstruction[14:11], MicroInstructionROM_microinstruction[10:9], MicroInstructionROM_microinstruction[8], MicroInstructionROM_microinstruction[7:6], MicroInstructionROM_microinstruction[5:0], instruction2register_1_p2, instruction2register_1_p3, instruction2register_1_p4, instruction2register_1_p5, or_3_out, CLK2, pipeline_register_1_p12, pipeline_register_1_p13, pipeline_register_1_p14[8], pipeline_register_1_p15, pipeline_register_1_p16, pipeline_register_1_p17, A_Etapa1, B_Etapa1, C_Etapa1
  Hex_Digit_Display hex_digit_display_31 (.value(register_bank_viewer_1_b_address_n0));  // open: dp
  LED led_5 (.in(pipeline_register_viewer_1_a_is_enabled));
  Hex_Digit_Display hex_digit_display_32 (.value(pipeline_register_viewer_1_a_lsn));  // open: dp
  Hex_Digit_Display hex_digit_display_33 (.value(pipeline_register_viewer_1_a_msn));  // open: dp
  // Probe on A_Etapa1
  // Probe on B_Etapa1
  // Probe on C_Etapa1
  register_bank register_bank_1 (
    .clk(CLK), .register_out_B_data(register_bank_1_register_out_b_data), .register_out_A_address(A_Etapa1),
    .register_out_B_address(B_Etapa1), .register_out_A_data(register_bank_1_register_out_a_data),
    .register_in_data(reg_C_write), .register_in_address(C_Etapa3));  // open: register_out_aux_address, register_out_aux_data
  LED led_6 (.in(pipeline_register_viewer_1_b_is_enabled));
  Hex_Digit_Display hex_digit_display_34 (.value(pipeline_register_viewer_1_b_lsn));  // open: dp
  Hex_Digit_Display hex_digit_display_35 (.value(pipeline_register_viewer_1_b_msn));  // open: dp
  // Probe on C_Etapa3
  // UC1 uc1_1: pin names not known; wires that end beside it: HOLD, pipeline_register_1_p15, not_1_out, mem_is_free, uc1_1_p5, uc1_1_p6, LatchMemEnable, UC1_HOLD
  Register #(.width(1)) register_1 (.D(uc1_1_p5), .clk(CLK2), .Q(register_1_q));  // open: en, clr
  Register #(.width(16), .trigger("falling")) Constant_K (
    .D(instruction2register_1_p6), .clk(CLK2), .Q(Constant_K_q));  // open: en, clr
  Register #(.width(1), .trigger("falling")) register_2 (.D(uc1_1_p6), .clk(CLK2), .Q(register_2_q));  // open: en, clr
  not not_2 (not_2_out, pipeline_register_1_p14[8]);
  Register #(.width(16)) BusA_ALU (.D(multiplexer_1_out), .en(uc1_1_p5), .clk(CLK2), .Q(BusA_ALU_q));  // open: clr
  Multiplexer #(.width(16), .enable("false")) multiplexer_1 (
    .in0(Constant_K_q), .in1(register_bank_1_register_out_a_data), .out(multiplexer_1_out), .sel(not_2_out));
  Register #(.width(16)) BusB_ALU (
    .D(register_bank_1_register_out_b_data), .en(uc1_1_p5), .clk(CLK2), .Q(BusB_ALU_q));  // open: clr
  Register #(.width(10), .trigger("falling")) register_3 (
    .D(pipeline_register_1_p17), .en(uc1_1_p6), .clk(CLK2), .Q(register_3_q));  // open: clr
  DotMatrix #(.matrixcols(17), .matrixrows(4)) dotmatrix_6 (
    .col0(pipeline_register_viewer_2_b16), .col1(pipeline_register_viewer_2_b15),
    .col2(pipeline_register_viewer_2_b14), .col3(pipeline_register_viewer_2_b13),
    .col4(pipeline_register_viewer_2_b12), .col5(pipeline_register_viewer_2_b11),
    .col6(pipeline_register_viewer_2_b10), .col7(pipeline_register_viewer_2_b9),
    .col8(pipeline_register_viewer_2_b8), .col9(pipeline_register_viewer_2_b7),
    .col10(pipeline_register_viewer_2_b6), .col11(pipeline_register_viewer_2_b5),
    .col12(pipeline_register_viewer_2_b4), .col13(pipeline_register_viewer_2_b3),
    .col14(pipeline_register_viewer_2_b2), .col15(pipeline_register_viewer_2_b1),
    .col16(pipeline_register_viewer_2_b0));
  pipeline_register_viewer pipeline_register_viewer_2 (
    .b7(pipeline_register_viewer_2_b7), .b12(pipeline_register_viewer_2_b12),
    .A_is_enabled(pipeline_register_viewer_2_a_is_enabled), .A_LSN(pipeline_register_viewer_2_a_lsn),
    .b16(pipeline_register_viewer_2_b16), .b11(pipeline_register_viewer_2_b11),
    .b2(pipeline_register_viewer_2_b2), .b3(pipeline_register_viewer_2_b3),
    .b8(pipeline_register_viewer_2_b8), .C_in(C_Etapa2Alu), .B_MSN(pipeline_register_viewer_2_b_msn),
    .microinstruction({ALU_Pipeline_p12, ALU_Pipeline_p13, ALU_Pipeline_p14[8], MREtapa2Pipeline, ALU_Pipeline_p16}),
    .b15(pipeline_register_viewer_2_b15), .b14(pipeline_register_viewer_2_b14),
    .b1(pipeline_register_viewer_2_b1), .b4(pipeline_register_viewer_2_b4),
    .b13(pipeline_register_viewer_2_b13), .B_in(ALU_Pipeline_p19),
    .B_is_enabled(pipeline_register_viewer_2_b_is_enabled), .A_in(ALU_Pipeline_p18),
    .b10(pipeline_register_viewer_2_b10), .b5(pipeline_register_viewer_2_b5),
    .b0(pipeline_register_viewer_2_b0), .b9(pipeline_register_viewer_2_b9),
    .b6(pipeline_register_viewer_2_b6), .A_MSN(pipeline_register_viewer_2_a_msn),
    .B_LSN(pipeline_register_viewer_2_b_lsn), .C_is_enabled(pipeline_register_viewer_2_c_is_enabled),
    .C_MSN(pipeline_register_viewer_2_c_msn), .C_LSN(pipeline_register_viewer_2_c_lsn));
  not not_3 (not_3_out, uc1_1_p5);
  and and_1 (and_1_out, ~CLK3, register_2_q);  // AND_Gate
  Register #(.width(16), .trigger("falling")) BusA_LS (
    .D(register_bank_1_register_out_a_data), .en(uc1_1_p6), .clk(CLK2), .Q(BusA_LS_q));  // open: clr
  // Probe on BusA_ALU_q
  // Probe on BusB_ALU_q
  DotMatrix #(.matrixcols(17), .matrixrows(4)) dotmatrix_7 (
    .col0(pipeline_register_viewer_3_b16), .col1(pipeline_register_viewer_3_b15),
    .col2(pipeline_register_viewer_3_b14), .col3(pipeline_register_viewer_3_b13),
    .col4(pipeline_register_viewer_3_b12), .col5(pipeline_register_viewer_3_b11),
    .col6(pipeline_register_viewer_3_b10), .col7(pipeline_register_viewer_3_b9),
    .col8(pipeline_register_viewer_3_b8), .col9(pipeline_register_viewer_3_b7),
    .col10(pipeline_register_viewer_3_b6), .col11(pipeline_register_viewer_3_b5),
    .col12(pipeline_register_viewer_3_b4), .col13(pipeline_register_viewer_3_b3),
    .col14(pipeline_register_viewer_3_b2), .col15(pipeline_register_viewer_3_b1),
    .col16(pipeline_register_viewer_3_b0));
  pipeline_register_viewer pipeline_register_viewer_3 (
    .b7(pipeline_register_viewer_3_b7), .b12(pipeline_register_viewer_3_b12),
    .A_is_enabled(pipeline_register_viewer_3_a_is_enabled), .A_LSN(pipeline_register_viewer_3_a_lsn),
    .b16(pipeline_register_viewer_3_b16), .b11(pipeline_register_viewer_3_b11),
    .b2(pipeline_register_viewer_3_b2), .b3(pipeline_register_viewer_3_b3),
    .b8(pipeline_register_viewer_3_b8), .C_in(C_Etapa2Mem), .B_MSN(pipeline_register_viewer_3_b_msn),
    .microinstruction({LoadStore_p16[14:8], MRMW, LoadStore_p16[5:0]}), .b15(pipeline_register_viewer_3_b15),
    .b14(pipeline_register_viewer_3_b14), .b1(pipeline_register_viewer_3_b1),
    .b4(pipeline_register_viewer_3_b4), .b13(pipeline_register_viewer_3_b13), .B_in(LoadStore_p19),
    .B_is_enabled(pipeline_register_viewer_3_b_is_enabled), .A_in(LoadStore_p18),
    .b10(pipeline_register_viewer_3_b10), .b5(pipeline_register_viewer_3_b5),
    .b0(pipeline_register_viewer_3_b0), .b9(pipeline_register_viewer_3_b9),
    .b6(pipeline_register_viewer_3_b6), .A_MSN(pipeline_register_viewer_3_a_msn),
    .B_LSN(pipeline_register_viewer_3_b_lsn), .C_is_enabled(pipeline_register_viewer_3_c_is_enabled),
    .C_MSN(pipeline_register_viewer_3_c_msn), .C_LSN(pipeline_register_viewer_3_c_lsn));
  not not_4 (not_4_out, uc1_1_p6);
  Register #(.width(1)) register_4 (.D(ALUALULAU_cyout), .en(1'b1), .clk(CLK2), .Q(CYin));  // open: clr
  LED led_7 (.in(pipeline_register_viewer_2_c_is_enabled));
  Hex_Digit_Display hex_digit_display_36 (.value(pipeline_register_viewer_2_c_msn));  // open: dp
  or or_4 (or_4_out, mem_is_free, nor_1_out);
  nor nor_1 (nor_1_out, mem_is_free, MEM_is_done);
  and and_2 (and_2_out, register_1_q, CLK3);
  ALU ALUALULAU (
    .ALUC(ALU_Pipeline_p12), .A(BusA_ALU_q), .B(BusB_ALU_q), .CYin(CYin), .Z(ALUALULAU_z),
    .CYout(ALUALULAU_cyout));
  LED led_8 (.in(pipeline_register_viewer_2_a_is_enabled));
  Hex_Digit_Display hex_digit_display_37 (.value(pipeline_register_viewer_2_c_lsn));  // open: dp
  Hex_Digit_Display hex_digit_display_38 (.value(pipeline_register_viewer_2_a_msn));  // open: dp
  // Pipeline_register ALU_Pipeline: pin names not known; wires that end beside it: pipeline_register_1_p12, pipeline_register_1_p13, pipeline_register_1_p14[8], pipeline_register_1_p15, pipeline_register_1_p16, pipeline_register_1_p17, A_Etapa1, B_Etapa1, C_Etapa1, not_3_out, CLK3, ALU_Pipeline_p12, ALU_Pipeline_p13, ALU_Pipeline_p14[8], MREtapa2Pipeline, ALU_Pipeline_p16, ALU_Pipeline_p17, ALU_Pipeline_p18, ALU_Pipeline_p19, C_Etapa2Alu
  and and_3 (and_3_out, ~uc1_1_p5, or_4_out);  // AND_Gate
  // Probe on ALUALULAU_z
  LED led_9 (.in(pipeline_register_viewer_3_c_is_enabled));
  Hex_Digit_Display hex_digit_display_39 (.value(pipeline_register_viewer_3_c_lsn));  // open: dp
  Hex_Digit_Display hex_digit_display_40 (.value(pipeline_register_viewer_3_c_msn));  // open: dp
  // Pipeline_register LoadStore: pin names not known; wires that end beside it: pipeline_register_1_p12, pipeline_register_1_p13, pipeline_register_1_p14[8], pipeline_register_1_p15, pipeline_register_1_p16, pipeline_register_1_p17, A_Etapa1, B_Etapa1, C_Etapa1, not_4_out, CLK3, LoadStore_p16[14:11], LoadStore_p16[10:9], LoadStore_p16[8], MRMW, LoadStore_p16[5:0], LoadStore_p17, LoadStore_p18, LoadStore_p19, C_Etapa2Mem
  and and_4 (and_4_out, MEM_is_done, ~mem_is_free);  // AND_Gate
  Hex_Digit_Display hex_digit_display_41 (.value(pipeline_register_viewer_2_a_lsn));  // open: dp
  Hex_Digit_Display hex_digit_display_42 (.value(pipeline_register_viewer_2_b_msn));  // open: dp
  Register #(.width(16)) register_5 (.D(ALUALULAU_z), .en(1'b1), .clk(CLK2), .Q(ALU_RESULT));  // open: clr
  LED led_10 (.in(pipeline_register_viewer_3_a_is_enabled));
  Hex_Digit_Display hex_digit_display_43 (.value(pipeline_register_viewer_3_a_msn));  // open: dp
  Hex_Digit_Display hex_digit_display_44 (.value(pipeline_register_viewer_3_a_lsn));  // open: dp
  Data data_1 (
    .DAddress(register_3_q), .M(MRMW), .clk(CLK2), .Enable(register_2_q), .DataMemInput(BusA_LS_q),
    .DataMemOut(data_1_datamemout));
  LED led_11 (.in(pipeline_register_viewer_2_b_is_enabled));
  Hex_Digit_Display hex_digit_display_45 (.value(pipeline_register_viewer_2_b_lsn));  // open: dp
  LED led_12 (.in(pipeline_register_viewer_3_b_is_enabled));
  Hex_Digit_Display hex_digit_display_46 (.value(pipeline_register_viewer_3_b_msn));  // open: dp
  // Probe on MRMW
  // Probe on LoadStore_p17
  // Probe on data_1_datamemout
  ALU_unit_control alu_unit_control_1 (
    .set_free(and_3_out), .set_not_free(and_2_out), .clk(CLK3), .is_free(ALU_is_free), .is_done(ALU_is_done));
  Hex_Digit_Display hex_digit_display_47 (.value(pipeline_register_viewer_3_b_lsn));  // open: dp
  // Probe on mem_is_free
  memory_unit_control memory_unit_control_1 (
    .set_free(and_4_out), .set_not_free(and_1_out), .clk(CLK2), .is_free(mem_is_free), .is_done(MEM_is_done));
  Register #(.width(16)) register_6 (.D(data_1_datamemout), .en(1'b1), .clk(CLK2), .Q(register_6_q));  // open: clr
  DotMatrix #(.matrixcols(17), .matrixrows(4)) dotmatrix_8 (
    .col0(pipeline_register_viewer_4_b16), .col1(pipeline_register_viewer_4_b15),
    .col2(pipeline_register_viewer_4_b14), .col3(pipeline_register_viewer_4_b13),
    .col4(pipeline_register_viewer_4_b12), .col5(pipeline_register_viewer_4_b11),
    .col6(pipeline_register_viewer_4_b10), .col7(pipeline_register_viewer_4_b9),
    .col8(pipeline_register_viewer_4_b8), .col9(pipeline_register_viewer_4_b7),
    .col10(pipeline_register_viewer_4_b6), .col11(pipeline_register_viewer_4_b5),
    .col12(pipeline_register_viewer_4_b4), .col13(pipeline_register_viewer_4_b3),
    .col14(pipeline_register_viewer_4_b2), .col15(pipeline_register_viewer_4_b1),
    .col16(pipeline_register_viewer_4_b0));
  pipeline_register_viewer pipeline_register_viewer_4 (
    .b7(pipeline_register_viewer_4_b7), .b12(pipeline_register_viewer_4_b12),
    .A_is_enabled(pipeline_register_viewer_4_a_is_enabled), .A_LSN(pipeline_register_viewer_4_a_lsn),
    .b16(pipeline_register_viewer_4_b16), .b11(pipeline_register_viewer_4_b11),
    .b2(pipeline_register_viewer_4_b2), .b3(pipeline_register_viewer_4_b3),
    .b8(pipeline_register_viewer_4_b8), .C_in(C_Etapa3), .B_MSN(pipeline_register_viewer_4_b_msn),
    .microinstruction(pipeline_register_2_p15), .b15(pipeline_register_viewer_4_b15),
    .b14(pipeline_register_viewer_4_b14), .b1(pipeline_register_viewer_4_b1),
    .b4(pipeline_register_viewer_4_b4), .b13(pipeline_register_viewer_4_b13), .B_in(pipeline_register_2_p17),
    .B_is_enabled(pipeline_register_viewer_4_b_is_enabled), .A_in(pipeline_register_2_p16),
    .b10(pipeline_register_viewer_4_b10), .b5(pipeline_register_viewer_4_b5),
    .b0(pipeline_register_viewer_4_b0), .b9(pipeline_register_viewer_4_b9),
    .b6(pipeline_register_viewer_4_b6), .A_MSN(pipeline_register_viewer_4_a_msn),
    .B_LSN(pipeline_register_viewer_4_b_lsn), .C_is_enabled(pipeline_register_viewer_4_c_is_enabled),
    .C_MSN(pipeline_register_viewer_4_c_msn), .C_LSN(pipeline_register_viewer_4_c_lsn));
  Multiplexer #(.width(16), .enable("false")) multiplexer_2 (
    .in0(ALU_RESULT), .in1(register_6_q), .out(reg_C_write), .sel(MEM_is_done));
  LED led_13 (.in(pipeline_register_viewer_4_c_is_enabled));
  Hex_Digit_Display hex_digit_display_48 (.value(pipeline_register_viewer_4_c_msn));  // open: dp
  Hex_Digit_Display hex_digit_display_49 (.value(pipeline_register_viewer_4_c_lsn));  // open: dp
  judge judge_1 (
    .reg_in_alu({ALU_Pipeline_p12, ALU_Pipeline_p13, ALU_Pipeline_p14[8], MREtapa2Pipeline, ALU_Pipeline_p16}),
    .reg_in_memory({LoadStore_p16[14:8], MRMW, LoadStore_p16[5:0]}), .A_alu(ALU_Pipeline_p18),
    .A_mem(LoadStore_p18), .B_alu(ALU_Pipeline_p19), .B_mem(LoadStore_p19), .C_alu(C_Etapa2Alu),
    .C_mem(C_Etapa2Mem), .in_9({MEM_is_done, ALU_is_done}), .reg_out(judge_1_reg_out), .A_bus(judge_1_a_bus),
    .B_bus(judge_1_b_bus), .C_bus(judge_1_c_bus));
  LED led_14 (.in(pipeline_register_viewer_4_a_is_enabled));
  Hex_Digit_Display hex_digit_display_50 (.value(pipeline_register_viewer_4_a_lsn));  // open: dp
  Hex_Digit_Display hex_digit_display_51 (.value(pipeline_register_viewer_4_a_msn));  // open: dp
  LED led_15 (.in(pipeline_register_viewer_4_b_is_enabled));
  Hex_Digit_Display hex_digit_display_52 (.value(pipeline_register_viewer_4_b_msn));  // open: dp
  Hex_Digit_Display hex_digit_display_53 (.value(pipeline_register_viewer_4_b_lsn));  // open: dp
  UC2 uc2_1 (
    .A_etapa_1(A_Etapa1), .B_etapa_1(B_Etapa1), .C_etapa_1(C_Etapa1), .C_etapa_2_ALU(C_Etapa2Alu),
    .ALU_is_done(ALU_is_free), .C_etapa_2_MEM(C_Etapa2Mem), .MEM_is_done(mem_is_free), .C_etapa_3(C_Etapa3),
    .clk(CLK), .out_10(HOLD));
  UC2_viewer uc2_viewer_2 (
    .out_7(uc2_viewer_2_out_7), .out_5(uc2_viewer_2_out_5), .out_3(uc2_viewer_2_out_3), .hold(HOLD),
    .out_6(uc2_viewer_2_out_6), .out_9(uc2_viewer_2_out_9), .out_8(uc2_viewer_2_out_8),
    .out_2(uc2_viewer_2_out_2), .out_4(uc2_viewer_2_out_4));
  DotMatrix #(.matrixcols(8), .matrixrows(8)) dotmatrix_9 (
    .col0(uc2_viewer_2_out_2), .col1(uc2_viewer_2_out_3), .col2(uc2_viewer_2_out_4),
    .col3(uc2_viewer_2_out_5), .col4(uc2_viewer_2_out_6), .col5(uc2_viewer_2_out_7),
    .col6(uc2_viewer_2_out_8), .col7(uc2_viewer_2_out_9));
  // Pipeline_register pipeline_register_2: pin names not known; wires that end beside it: judge_1_reg_out[14:11], judge_1_reg_out[10:9], judge_1_reg_out[8], judge_1_reg_out[7:6], judge_1_reg_out[5:0], judge_1_c_bus, pipeline_register_2_p7, CLK3, judge_1_a_bus, judge_1_b_bus, pipeline_register_2_p15[14:11], pipeline_register_2_p15[10:9], pipeline_register_2_p15[8], pipeline_register_2_p15[7:6], pipeline_register_2_p15[5:0], pipeline_register_2_p16, pipeline_register_2_p17, C_Etapa3
  // NOT_Gate not_5 is placed but not wired

  // Other names for the same wires on the sheet: pulseGenManual = in_1; reg_C_address[5:0] = C_Etapa3

  // Notes on the sheet:
  //   contents of ProgramMemory (hex, n*v repeats v):
  //   9c3dfe 82223f 8849ff 933329 200061 300029 822222 822223 822224 822225 822226 822227 822228 822229
  //   82222a 82222b 82222c 82222d 82222e 82222f 822230 200070 80c85 3000aa
  //   PC
  //   splitters que encajar con los registros de pipeline
  //   para hacer copy-paste
  //   probes que encajar en los splitters de arriba
  //   INSTRUCTION
  //   REGISTER
  //   Y USAR EL DISPLAY EN LOS PUERTOS DE SALIDA PO0 Y PO1
  //   LA IDEA ES USAR LOS DIP SWITCH EN LOS PUERTOS DE ENTRADA PI0 Y PI1
  //   ESTA CONEXION ES SOLO DE PRUEBA
  //   Detecto nueva operacion de memoria
  //   El mux es el de los is_done , el menos significativo es el de la ALU que se pone en 1 cuando termino
endmodule
