// Logisim project ALU_ALU.circ as structural Verilog: 3 circuits, main circuit ALU
module ALU (
  input  [15:0] A,
  input  [15:0] B,
  input  CYin,
  input  [3:0] ALUC,
  output CYout,
  output [15:0] Z
);

  wire CYin_t, multiplexer_1_out, multiplexer_2_out, undriven, undriven_2, undriven_3, undriven_4;
  wire [15:0] AandB, AorB, CY0, CY1, notA, notB, sumAB, undriven_5, Z0, Z0xFFFF, Z1;

  assign notA = ~A;  // NOT_Gate not_1, 16 bits wide
  assign notB = ~B;  // NOT_Gate not_2, 16 bits wide
  Multiplexer #(.enable("false")) multiplexer_1 (
    .in0(undriven), .in1(undriven_2), .out(multiplexer_1_out));  // open: sel
  Multiplexer #(.enable("false")) multiplexer_2 (
    .in0(undriven_3), .in1(undriven_4), .out(multiplexer_2_out));  // open: sel
  // ALU_full_adder_16 alu_full_adder_16_1: pin names not known; wires that end beside it: multiplexer_1_out, multiplexer_2_out, CYin_t, sumAB, CYout
  Multiplexer #(.select(4), .width(16), .enable("false")) multiplexer_3 (
    .in0(A), .in1(B), .in2(notA), .in3(notB), .in4(sumAB), .in5(sumAB), .in6(AorB), .in7(AandB), .in8(Z0),
    .in9(Z1), .in10(Z0xFFFF), .in11(CY0), .in12(CY1), .in13(undriven_5), .in14(undriven_5),
    .in15(undriven_5), .out(Z));  // open: sel
  Multiplexer #(.select(3), .width(16), .enable("false")) multiplexer_4 ();  // open: in0, in1, in2, in3, in4, in5, in6, in7, out, sel

  // Notes on the sheet:
  //   Este suma AB con Carry
endmodule

module ALU_full_adder (
  input  Xin,
  input  Yin,
  input  Cin,
  output SUMout,
  output Cout
);

  wire and_1_out, and_2_out, xor_1_out;

  xor xor_1 (xor_1_out, Xin, Yin);
  and and_1 (and_1_out, xor_1_out, Cin);
  and and_2 (and_2_out, Yin, Xin);
  xor xor_2 (SUMout, xor_1_out, Cin);
  or or_1 (Cout, and_1_out, and_2_out);
endmodule

module ALU_full_adder_16 (
  input  [15:0] Ain,
  input  [15:0] Bin,
  input  Carryin,
  output [15:0] SUM_out,
  output Carry_out
);

  wire C0, C1, C2, C3, C4, C5, C6, C7, C8, C9, C10, C11, C12, C13, C14;

  ALU_full_adder alu_full_adder_1 (.Xin(Ain[0]), .Yin(Bin[0]), .Cin(Carryin), .SUMout(SUM_out[0]), .Cout(C0));
  ALU_full_adder alu_full_adder_2 (.Xin(Ain[1]), .Yin(Bin[1]), .Cin(C0), .SUMout(SUM_out[1]), .Cout(C1));
  ALU_full_adder alu_full_adder_3 (.Xin(Ain[2]), .Yin(Bin[2]), .Cin(C1), .SUMout(SUM_out[2]), .Cout(C2));
  ALU_full_adder alu_full_adder_4 (.Xin(Ain[3]), .Yin(Bin[3]), .Cin(C2), .SUMout(SUM_out[3]), .Cout(C3));
  ALU_full_adder alu_full_adder_5 (.Xin(Ain[4]), .Yin(Bin[4]), .Cin(C3), .SUMout(SUM_out[4]), .Cout(C4));
  ALU_full_adder alu_full_adder_6 (.Xin(Ain[5]), .Yin(Bin[5]), .Cin(C4), .SUMout(SUM_out[5]), .Cout(C5));
  ALU_full_adder alu_full_adder_7 (.Xin(Ain[6]), .Yin(Bin[6]), .Cin(C5), .SUMout(SUM_out[6]), .Cout(C6));
  ALU_full_adder alu_full_adder_8 (.Xin(Ain[7]), .Yin(Bin[7]), .Cin(C6), .SUMout(SUM_out[7]), .Cout(C7));
  ALU_full_adder alu_full_adder_9 (.Xin(Ain[8]), .Yin(Bin[8]), .Cin(C7), .SUMout(SUM_out[8]), .Cout(C8));
  ALU_full_adder alu_full_adder_10 (.Xin(Ain[9]), .Yin(Bin[9]), .Cin(C8), .SUMout(SUM_out[9]), .Cout(C9));
  ALU_full_adder alu_full_adder_11 (.Xin(Ain[10]), .Yin(Bin[10]), .Cin(C9), .SUMout(SUM_out[10]), .Cout(C10));
  ALU_full_adder alu_full_adder_12 (.Xin(Ain[11]), .Yin(Bin[11]), .Cin(C10), .SUMout(SUM_out[11]), .Cout(C11));
  ALU_full_adder alu_full_adder_13 (.Xin(Ain[12]), .Yin(Bin[12]), .Cin(C11), .SUMout(SUM_out[12]), .Cout(C12));
  ALU_full_adder alu_full_adder_14 (.Xin(Ain[13]), .Yin(Bin[13]), .Cin(C12), .SUMout(SUM_out[13]), .Cout(C13));
  ALU_full_adder alu_full_adder_15 (.Xin(Ain[14]), .Yin(Bin[14]), .Cin(C13), .SUMout(SUM_out[14]), .Cout(C14));
  ALU_full_adder alu_full_adder_16 (.Xin(Ain[15]), .Yin(Bin[15]), .Cin(C14), .SUMout(SUM_out[15]), .Cout(Carry_out));

  // Other names for the same wires on the sheet: A0 = Ain[0]; A1 = Ain[1]; A2 = Ain[2]; A3 = Ain[3]; A4 = Ain[4];
  //   A5 = Ain[5]; A6 = Ain[6]; A7 = Ain[7]; A8 = Ain[8]; A9 = Ain[9]; A10 = Ain[10]; A11 = Ain[11]; A12 = Ain[12];
  //   A13 = Ain[13]; A14 = Ain[14]; A15 = Ain[15]; B0 = Bin[0]; B1 = Bin[1]; B2 = Bin[2]; B3 = Bin[3]; B4 = Bin[4];
  //   B5 = Bin[5]; B6 = Bin[6]; B7 = Bin[7]; B8 = Bin[8]; B9 = Bin[9]; B10 = Bin[10]; B11 = Bin[11]; B12 = Bin[12];
  //   B13 = Bin[13]; B14 = Bin[14]; B15 = Bin[15]; Cin = Carryin; Cout = Carry_out
endmodule
