// Logisim project PCReg.circ as structural Verilog: 1 circuit, main circuit PCreg
module PCreg (
  input  Preload,
  input  CLK1,
  input  HOLD,
  input  [10:0] displacement_or_address,
  output [10:0] PC
);

  wire counter_1_carry, not_1_out;

  not not_1 (not_1_out, HOLD);
  Counter #(.width(11), .max('h7ff), .ongoal("continue"), .trigger("falling")) counter_1 (
    .load(Preload), .count(not_1_out), .clk(CLK1), .D(displacement_or_address), .carry(counter_1_carry),
    .Q(PC));  // open: clr, up
  // also tied to GND on the sheet: counter_1_carry
endmodule
