// Logisim project UC1.circ as structural Verilog: 1 circuit, main circuit UC1
module UC1 (
  input  HOLD,
  input  [1:0] MRyMW_OUT_E1,
  input  ALUisFree,
  input  MEMisFree,
  output ALUEnable,
  output LoadStoreEnable,
  output LatchMemEnable,
  output Hold2
);

  wire and_1_out, and_2_out, or_1_out;

  or or_1 (or_1_out, MRyMW_OUT_E1[0], MRyMW_OUT_E1[1]);
  and and_1 (and_1_out, ~MEMisFree, or_1_out);  // AND_Gate
  and and_2 (and_2_out, ~ALUisFree, ~or_1_out);  // AND_Gate
  and and_3 (ALUEnable, ~HOLD, ~or_1_out, ALUisFree);  // AND_Gate
  and and_4 (LoadStoreEnable, ~HOLD, or_1_out, MEMisFree);  // AND_Gate
  and and_5 (LatchMemEnable, ~HOLD, or_1_out);  // AND_Gate
  or or_2 (Hold2, and_1_out, and_2_out);
endmodule
